# Fritzing sketch Roktrack (saved by Fritzing 0.9.10b)

parts:
  MCU1 = Raspberry Pi A+
  U1 = TRANSCHIPTC5747 [package=camera_sfv24r-2st_2]  # not connected
  SP1 = SPEAKER [package=pcb_mount_speaker]  # not connected
  パーツ1 = 12 NeoPixel Ring [part_number=1643]
  S1 = D2F-FL Omron Snap Action Limit Switch with Level
  BAT1 = 12 battery [package=battery]
  M1 = gear-motor  # not connected
  M2 = gear-motor  # not connected
  M3 = DC Motor [voltage_(max)=6V voltage_(min)=3V]
  M4 = DC Motor [voltage_(max)=6V voltage_(min)=3V]
  Mod1 = Solar Charge Controller [part_number="KLD Series Solar Charge Controller PWM" package=PWM-Model]
  Part1 = Solar Panel [package="Renogy 50 Watts 12 Volt Monocrystalline Bendable Solar Panel"]
  U2 = LM2596 step down module  # not connected
  U3 = LM2596 step down module
  L298N1 = L298N DC motor driver
  A1 = 2 channel relay module [package=THT]
  S2 = Round Pushbutton
  F1 = Fan - Ventilador [package=THT]

nets:
  N1: MCU1.pin_1, MCU1.pin_17, M3.pin_1, M4.pin_1, Mod1.Connector_6, U3.IN-, U3.OUT-
  N2: MCU1.pin_2, MCU1.pin_4, U3.OUT+
  N3: MCU1.pin_8, A1.pin_15
  N4: MCU1.pin_9, MCU1.pin_39, S1.Pin_3
  N5: MCU1.pin_15, L298N1.IN1
  N6: MCU1.pin_16, L298N1.IN2
  N7: MCU1.pin_18, L298N1.IN3
  N8: MCU1.pin_22, L298N1.IN4
  N9: MCU1.pin_37, S1.Pin_2
  N10: MCU1.pin_40, パーツ1.OUT
  N11: BAT1.-, Mod1.Connector_4
  N12: BAT1.+, Mod1.Connector_3
  N13: M3.pin_2, M4.pin_2, A1.pin_1
  N14: Mod1.Connector_1, Part1.Connector_1
  N15: Mod1.Connector_2, Part1.Connector_2
  N16: Mod1.Connector_5, S2.leg0
  N17: U3.IN+, S2.leg1, F1.5V

custom parts:
  Raspberry Pi A+: The awesome Raspberry Pi ARM Board with 40 pin GPIO. Ready for special designed Raspberry Pi A+ Hat (Hardware attached (on) top). Jan 2018: Cloned from the B+ version, and modified to match the official I/O pin numbers with a totally new schematic.
  12 NeoPixel Ring: 12 ultra bright smart LED NeoPixels are arranged in a circle with 1.5" (37mm) outer diameter. The rings are 'chainable' - connect the output pin of one to the input pin of another. Use only one microcontroller pin to control as many as you can chain together! Each LED is addressable as the driver chip is inside the LED. Each one has ~18mA constant current drive so the color will be very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
  D2F-FL Omron Snap Action Limit Switch with Level: Snap action switch with stainless steel lever.
  12 battery: 12V lead acid type battery, like the Husqvarna YTH2448 12V 35AH battery. This is the mini version 1/4 the size of the actual battery to be closer to typical breadboard parts (around 2in wide rathher than 7in). The pads in pcb are sized to accomidate up to 14ga wire (as these batterys will deliver high currents.)
  Solar Charge Controller: PWM-Solar Charge Controller
  Solar Panel: Renogy 50 Watts 12 Volt Solar Panel
  LM2596 step down module: LM2596 DC-DC step down power supply module 3 A.
  L298N DC motor driver: 2x DC motor driver with 78M05 positive voltage regulator (7..35 V) L298N: max 46 V, 2 A Set 5 V Enable jumper to enable 5 V regultor (needed for the L298N) and +5 V output at screw terminal or supply external +5 V at screw terminal Set ENA and/or ENB to +5 V to enable motor permanently or supply ENA and/or ENB with PWM signal IN1 and IN2 set rotation directory for motor A (OUT1/OUT2) IN2 and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
  2 channel relay module: 2 channel Relay Module 5V 12V 24V High and Low Level Trigger Relay Control With Optocoupler Two Way relays DC 5 V 12 V 24 V Volt.
  Fan - Ventilador: Ventilador de 2 pines, se encuentra comunmente en computadoras de escritorio
